// Logisim project memory.circ as structural Verilog: 1 circuit, main circuit memory
module memory (
  input  Register_In,
  input  Register_Load,
  input  Register_Clock,
  input  Register_Clear,
  input  DT_FlipFlop_Clock,
  input  DT_FlipFlop_Data,
  input  DT_FlipFlop_Load,
  output Register_Out,
  output D_Q1,
  output D_Q0,
  output T_Q1,
  output T_Q0
);

  Register #(.width(1)) register_1 (
    .D(Register_In), .en(Register_Load), .Q(Register_Out), .clk(Register_Clock), .clr(Register_Clear));
  D_Flip_Flop d_ff_1 (
    .clk(DT_FlipFlop_Clock), .D(DT_FlipFlop_Data), .Q(D_Q1), .Qn(D_Q0), .en(DT_FlipFlop_Load));  // open: preset, reset
  T_Flip_Flop t_ff_1 (
    .clk(DT_FlipFlop_Clock), .T(DT_FlipFlop_Data), .Q(T_Q1), .Qn(T_Q0), .en(DT_FlipFlop_Load));  // open: preset, reset
endmodule
